# Fritzing sketch open-aquarium (saved by Fritzing 0.9.4)
breadboards: 3

parts:
  Part1 = Arduino Mega 2560 (Rev3)
  LED1 = LED - 5mm [color="Red (633nm)" package="5 mm [THT]"]
  R1 = Resistor [tolerance=±5% resistance=470 package="2010 [SMD]"]
  DHT2 = DHT22 Humidity and Temperature Sensor
  R4 = Resistor [tolerance=±5% resistance=10k package="0805 [SMD]"]
  R5 = Rotary Potentiometer (Large) [maximum_resistance=100kΩ package=THT]
  Part3 = OLED Monochrome 128x64 1.3 inch [part_number=938]
  microSD = MicroSD Card Module
  DS3231-RTC = Adafruit PCF8523 RTC [part_number="Adafruit #3295"]
  SoundSensor = Adafruit MAX4466 Electret Microphone Amplifier [part_number="Adafruit #1063"]
  BMP280 = Adafruit_BMP280

nets:
  N1: Part1.D21/SCL, Part1.SCL, DS3231-RTC.SQW, DS3231-RTC.SCL, BMP280.SCK/SCL
  N2: Part1.D20/SDA, Part1.SDA, DS3231-RTC.SDA, BMP280.SDO/ADR
  GND: Part1.GND, LED1.cathode, R5.wiper, Part3.MOSI_SDA, microSD.GND, DS3231-RTC.GND, SoundSensor.GND, BMP280.GND
  N3: Part1.D13_PWM, R1.Pin_0
  3V3: Part1.3V3, BMP280.3.3V
  VCC: Part1.5V, DHT2.VDD, R4.Pin_0, R5.leg2, Part3.SCLK_SCK, microSD.VCC, DS3231-RTC.VCC, SoundSensor.VCC
  N4: Part1.D2_PWM, DHT2.DATA, R4.Pin_1
  N5: Part1.D3_PWM, R5.leg1
  N6: Part1.D4_PWM, SoundSensor.OUT
  N7: Part1.D22, Part3.DC_SA0
  N8: Part1.D23, Part3.RESET
  N9: Part1.D24, Part3.CS
  N10: Part1.D25, Part3.3.3V
  N11: Part1.D26, Part3.VIN
  N12: Part1.D50, microSD.MISO
  N13: Part1.D51, microSD.MOSI
  N14: Part1.D52, microSD.SCK
  N15: Part1.D53, microSD.CS
  N16: LED1.anode, R1.Pin_1

notes:
  Potentiometer Illustration:
  Photocell module
  Terminal 1: DO
  Terminal 2: GND
  Terminal 3: VCC

custom parts:
  OLED Monochrome 128x64 1.3 inch: These displays are small, only about 1.3" diagonal, but very readable due to the high contrast of an OLED display. This display is made of 128x64 individual white OLED pixels, each one is turned on or off by the controller chip. Because the display makes its own light, no backlight is required. This reduces the power required to run the OLED and is why the display has such high contrast; we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
  Adafruit PCF8523 RTC: This is a great battery-backed real time clock (RTC) that allows your microcontroller project to keep track of time even if it is reprogrammed, or if the power is lost. Perfect for datalogging, clock-building, time stamping, timers and alarms, etc. Equipped with PCF8523 RTC - it can run from 3.3V or 5V power & logic! Works great with an Arduino using our RTC library, with CircuitPython or with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
  Adafruit MAX4466 Electret Microphone Amplifier: Add an ear to your project with this well-designed electret microphone amplifier. This fully assembled and tested board comes with a 20-20KHz electret microphone soldered on. For the amplification, we use the Maxim MAX4466, an op-amp specifically designed for this delicate task! The amplifier has excellent power supply noise rejection, so this amplifier sounds really good and isn't nearly as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
  Adafruit_BMP280: Bosch has stepped up their game with their new BMP280 sensor, an environmental sensor with temperature, barometric pressure that is the next generation upgrade to the BMP085/BMP180/BMP183. This sensor is great for all sorts of weather sensing and can even be used in both I2C and SPI! This precision sensor from Bosch is the best low-cost, precision sensing solution for measuring barometric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

// code stored in the sketch: Untitled2.ino
void setup()
{
  Serial.begin(9600);
  pinMode(13, OUTPUT);
}

void loop()
{
  
  Serial.print("DATA ");
  digitalWrite(13, HIGH);
  delay(1000); // Wait for 1000 millisecond(s)
  // turn the LED off by making the voltage LOW
  digitalWrite(13, LOW);
  delay(1000); // Wait for 1000 millisecond(s)
}
